// Digital circuit part_c.dig as structural Verilog
module part_c (
);

  wire diodeforward_2_out, nfet_1_s, nfet_2_s, pfet_1_d, pfet_1_s, undriven, undriven_2;

  PFET pfet_1 (.G(undriven_2), .S(pfet_1_s), .D(pfet_1_d));
  DiodeForward diodeforward_1 (.out(pfet_1_s));  // open: in
  NFET nfet_1 (.G(undriven_2), .D(pfet_1_d), .S(nfet_1_s));
  NFET nfet_2 (.G(undriven), .D(nfet_1_s), .S(nfet_2_s));
  DiodeBackward diodebackward_1 (.out(nfet_2_s));  // open: in
  DiodeForward diodeforward_2 (.out(diodeforward_2_out));  // open: in
  PFET pfet_2 (.G(undriven), .S(diodeforward_2_out), .D(pfet_1_d));

  // Notes on the sheet:
  //   NAND
  //   NOR
endmodule
